# Fritzing sketch pong (saved by Fritzing 0.5.2b)
breadboards: 1

parts:
  Arduino1 = Arduino
  Right_input_control = Trimmer Potentiometer [package=THT]
  Left_input_control = Trimmer Potentiometer [package=THT]
  U1 = 74HC595 [package="DIP16 [THT]"]
  U2 = 74HC595 [package="DIP16 [THT]"]
  U3 = mystery part, 8 pins [chip_label="Nokia LCD" spacing=300mil]
  U4 = mystery part, 24 pins [chip_label="8x8 Led Matrix" spacing=300mil]

nets:
  GND: Arduino1.GND, Right_input_control.leg2, Left_input_control.leg2, U1.GND, U1.OE, U2.GND, U2.OE, U3.pin2
  N1: Arduino1.D12, U3.pin7
  N2: Arduino1.D11, U3.pin6
  N3: Arduino1.D10, U3.pin5
  N4: Arduino1.D9, U3.pin4
  N5: Arduino1.D8, U3.pin3
  N6: Arduino1.D4, U1.SH_CP, U2.SH_CP
  N7: Arduino1.D3, U1.ST_CP, U2.ST_CP
  N8: Arduino1.D2, U1.DS
  N9: Arduino1.3V3, U3.pin1
  VCC: Arduino1.+5V, Right_input_control.leg1, Left_input_control.leg1, U1.MR, U1.VCC, U2.MR, U2.VCC
  N10: Arduino1.A0, Right_input_control.wiper
  N11: Arduino1.A1, Left_input_control.wiper
  N12: U1.Q1, U4.pin19
  N13: U1.Q2, U4.pin18
  N14: U1.Q3, U4.pin17
  N15: U1.Q4, U4.pin16
  N16: U1.Q5, U4.pin15
  N17: U1.Q6, U4.pin14
  N18: U1.Q7, U4.pin13
  N19: U1.Q7', U2.DS
  N20: U1.Q0, U4.pin20
  N21: U2.Q1, U4.pin2
  N22: U2.Q2, U4.pin3
  N23: U2.Q3, U4.pin4
  N24: U2.Q4, U4.pin21
  N25: U2.Q5, U4.pin22
  N26: U2.Q6, U4.pin23
  N27: U2.Q7, U4.pin24
  N28: U2.Q0, U4.pin1
